// Logisim project guess-the-number.circ as structural Verilog: 7 circuits, main circuit main
module main (
  input  Jogar,
  input  A3,
  input  A2,
  input  A1,
  input  A0,
  input  Selecionar_jogador,
  input  B3,
  input  B2,
  input  B1,
  input  B0,
  output Correto,
  output \Número_secreto_é_menor ,
  output \Número_secreto_é_maior 
);

  wire decodificador_1_a_2, decodificador_1_b_2, decodificador_1_c_2, decodificador_1_d_2, decodificador_1_e,
       decodificador_1_f, decodificador_1_g, decodificador_2_a_2, decodificador_2_b_2, decodificador_2_c_2,
       decodificador_2_d_2, decodificador_2_e, decodificador_2_f, decodificador_2_g;

  _7_Segment_Display u_7_segment_display_1 (
    .g(decodificador_1_g), .f(decodificador_1_f), .a(decodificador_1_a_2), .b(decodificador_1_b_2),
    .e(decodificador_1_e), .d(decodificador_1_d_2), .c(decodificador_1_c_2));  // open: dp
  _7_Segment_Display u_7_segment_display_2 (
    .g(decodificador_2_g), .f(decodificador_2_f), .a(decodificador_2_a_2), .b(decodificador_2_b_2),
    .e(decodificador_2_e), .d(decodificador_2_d_2), .c(decodificador_2_c_2));  // open: dp
  Decodificador decodificador_1 (
    .a(A3), .b(A2), .c(A1), .d(A0), .a_2(decodificador_1_a_2), .b_2(decodificador_1_b_2),
    .c_2(decodificador_1_c_2), .d_2(decodificador_1_d_2), .e(decodificador_1_e), .f(decodificador_1_f),
    .g(decodificador_1_g));
  Decodificador decodificador_2 (
    .a(B3), .b(B2), .c(B1), .d(B0), .a_2(decodificador_2_a_2), .b_2(decodificador_2_b_2),
    .c_2(decodificador_2_c_2), .d_2(decodificador_2_d_2), .e(decodificador_2_e), .f(decodificador_2_f),
    .g(decodificador_2_g));
  Jogo jogo_1 (
    .in_1({A3, A2, A1, A0}), .Jogar(Jogar), .in_3({B3, B2, B1, B0}), .Selecionar_jogador(Selecionar_jogador),
    .Correto(Correto), .\Número_secreto_é_menor (\Número_secreto_é_menor ),
    .\Número_secreto_é_maior (\Número_secreto_é_maior ));

  // Notes on the sheet:
  //   Jogador 0
  //   Jogador 1
endmodule

module Teste (
  input  Selecionar_jogador,
  input  A3,
  input  A2,
  input  A1,
  input  A0,
  input  B3,
  input  B2,
  input  B1,
  input  B0,
  input  S3,
  input  S2,
  input  S1,
  input  S0,
  output Correto,
  output \Número_secreto_é_menor ,
  output \Número_secreto_é_maior 
);

  wire mux_2_1_1_c, mux_2_1_2_c, mux_2_1_3_c, mux_2_1_4_c;

  Hex_Digit_Display hex_digit_display_1 (.value({A3, A2, A1, A0}));  // open: dp
  Hex_Digit_Display hex_digit_display_2 (.value({B3, B2, B1, B0}));  // open: dp
  Mux_2_1 mux_2_1_1 (.Sel(Selecionar_jogador), .B(B3), .A(A3), .C(mux_2_1_1_c));
  Mux_2_1 mux_2_1_2 (.Sel(Selecionar_jogador), .B(B2), .A(A2), .C(mux_2_1_2_c));
  Mux_2_1 mux_2_1_3 (.Sel(Selecionar_jogador), .B(B1), .A(A1), .C(mux_2_1_3_c));
  Mux_2_1 mux_2_1_4 (.Sel(Selecionar_jogador), .B(B0), .A(A0), .C(mux_2_1_4_c));
  Comparador comparador_1 (
    .A3(mux_2_1_1_c), .A2(mux_2_1_2_c), .A1(mux_2_1_3_c), .A0(mux_2_1_4_c), .B3(S3), .B2(S2), .B1(S1),
    .B0(S0), .A_B(Correto), .A_B_2(\Número_secreto_é_menor ), .A_B_3(\Número_secreto_é_maior ));

  // Notes on the sheet:
  //   Jogador 0
  //   Jogador 1
  //   Número secreto
endmodule

module Mux_2_1 (
  input  Sel,
  input  B,
  input  A,
  output C
);

  wire and_1_out, and_2_out, and_3_out, and_4_out;

  and and_1 (and_1_out, Sel, B, ~A);  // AND_Gate
  and and_2 (and_2_out, A, ~B, ~Sel);  // AND_Gate
  and and_3 (and_3_out, A, B, ~Sel);  // AND_Gate
  and and_4 (and_4_out, A, B, Sel);
  or or_1 (C, and_1_out, and_2_out, and_3_out, and_4_out);
endmodule

module \Entradas_Binárias  (
  input  A0,
  input  A1,
  input  A2,
  input  A3,
  input  B0,
  input  B1,
  input  B2,
  input  B3,
  input  Sel,
  output out_10,
  output out_11,
  output out_12,
  output out_13
);

  wire decodificador_1_a_2, decodificador_1_b_2, decodificador_1_c_2, decodificador_1_d_2, decodificador_1_e,
       decodificador_1_f, decodificador_1_g, decodificador_2_a_2, decodificador_2_b_2, decodificador_2_c_2,
       decodificador_2_d_2, decodificador_2_e, decodificador_2_f, decodificador_2_g;

  _7_Segment_Display u_7_segment_display_1 (
    .g(decodificador_1_g), .f(decodificador_1_f), .a(decodificador_1_a_2), .b(decodificador_1_b_2),
    .e(decodificador_1_e), .d(decodificador_1_d_2), .c(decodificador_1_c_2));  // open: dp
  _7_Segment_Display u_7_segment_display_2 (
    .g(decodificador_2_g), .f(decodificador_2_f), .a(decodificador_2_a_2), .b(decodificador_2_b_2),
    .e(decodificador_2_e), .d(decodificador_2_d_2), .c(decodificador_2_c_2));  // open: dp
  Decodificador decodificador_1 (
    .a(A0), .b(A1), .c(A2), .d(A3), .a_2(decodificador_1_a_2), .b_2(decodificador_1_b_2),
    .c_2(decodificador_1_c_2), .d_2(decodificador_1_d_2), .e(decodificador_1_e), .f(decodificador_1_f),
    .g(decodificador_1_g));
  Decodificador decodificador_2 (
    .a(B0), .b(B1), .c(B2), .d(B3), .a_2(decodificador_2_a_2), .b_2(decodificador_2_b_2),
    .c_2(decodificador_2_c_2), .d_2(decodificador_2_d_2), .e(decodificador_2_e), .f(decodificador_2_f),
    .g(decodificador_2_g));
  Mux_2_1 mux_2_1_1 (.Sel(Sel), .B(B0), .A(A0), .C(out_10));
  Mux_2_1 mux_2_1_2 (.Sel(Sel), .B(B1), .A(A1), .C(out_11));
  Mux_2_1 mux_2_1_3 (.Sel(Sel), .B(B2), .A(A2), .C(out_12));
  Mux_2_1 mux_2_1_4 (.Sel(Sel), .B(B3), .A(A3), .C(out_13));
endmodule

module Decodificador (
  input  a,
  input  b,
  input  c,
  input  d,
  output a_2,
  output b_2,
  output c_2,
  output d_2,
  output e,
  output f,
  output g
);

  wire and_1_out, and_2_out, and_3_out, and_4_out, and_5_out, and_6_out, and_7_out, and_8_out, and_9_out,
       and_10_out, and_11_out, and_12_out, and_13_out, and_14_out, and_15_out, and_16_out, and_17_out,
       and_18_out, and_19_out, and_20_out, and_21_out, and_22_out, and_23_out, and_24_out, and_25_out,
       and_26_out, and_27_out, and_28_out, and_29_out, and_30_out, and_31_out, and_32_out, and_33_out,
       and_34_out;

  and and_1 (and_1_out, ~b, ~d);  // AND_Gate
  and and_2 (and_2_out, ~a, c);  // AND_Gate
  and and_3 (and_3_out, ~a, b, d);  // AND_Gate
  and and_4 (and_4_out, b, c);
  and and_5 (and_5_out, a, ~b, ~c);  // AND_Gate
  and and_6 (and_6_out, a, ~d);  // AND_Gate
  and and_7 (and_7_out, ~a, ~c, ~d);  // AND_Gate
  and and_8 (and_8_out, ~b, ~d);  // AND_Gate
  and and_9 (and_9_out, ~a, c, d);  // AND_Gate
  and and_10 (and_10_out, a, ~c, d);  // AND_Gate
  and and_11 (and_11_out, ~a, ~c, ~d);  // AND_Gate
  and and_12 (and_12_out, ~a, c, d);  // AND_Gate
  and and_13 (and_13_out, ~a, b);  // AND_Gate
  and and_14 (and_14_out, a, ~b);  // AND_Gate
  and and_15 (and_15_out, a, ~c, d);  // AND_Gate
  and and_16 (and_16_out, ~a, ~b, ~d);  // AND_Gate
  and and_17 (and_17_out, ~b, c, d);  // AND_Gate
  and and_18 (and_18_out, b, ~c, d);  // AND_Gate
  and and_19 (and_19_out, b, c, ~d);  // AND_Gate
  and and_20 (and_20_out, a, ~c);  // AND_Gate
  and and_21 (and_21_out, ~a, ~b, ~c);  // AND_Gate
  and and_22 (and_22_out, ~b, ~d);  // AND_Gate
  and and_23 (and_23_out, c, ~d);  // AND_Gate
  and and_24 (and_24_out, a, c);
  and and_25 (and_25_out, a, b);
  and and_26 (and_26_out, ~a, ~c);  // AND_Gate
  and and_27 (and_27_out, ~c, ~d);  // AND_Gate
  and and_28 (and_28_out, b, c);
  and and_29 (and_29_out, a, ~b);  // AND_Gate
  and and_30 (and_30_out, ~b, c);  // AND_Gate
  and and_31 (and_31_out, c, ~d);  // AND_Gate
  and and_32 (and_32_out, ~a, b, ~c);  // AND_Gate
  and and_33 (and_33_out, a, ~b);  // AND_Gate
  and and_34 (and_34_out, a, d);
  or or_1 (a_2, and_1_out, and_2_out, and_3_out, and_4_out, and_5_out, and_6_out);
  or or_2 (b_2, and_7_out, and_8_out, and_9_out, and_10_out);
  or or_3 (c_2, and_11_out, and_12_out, and_13_out, and_14_out, and_15_out);
  or or_4 (d_2, and_16_out, and_17_out, and_18_out, and_19_out, and_20_out);
  or or_5 (e, and_21_out, and_22_out, and_23_out, and_24_out, and_25_out);
  or or_6 (f, and_26_out, and_27_out, and_28_out, and_29_out);
  or or_7 (g, and_30_out, and_31_out, and_32_out, and_33_out, and_34_out);
endmodule

module Comparador (
  input  A3,
  input  A2,
  input  A1,
  input  A0,
  input  B3,
  input  B2,
  input  B1,
  input  B0,
  output A_B,
  output A_B_2,
  output A_B_3
);

  wire and_2_out, and_3_out, and_4_out, and_out, X0_out, X1_out, X2_out, X3_out;

  xnor X3 (X3_out, A3, B3);
  xnor X2 (X2_out, A2, B2);
  xnor X1 (X1_out, A1, B1);
  xnor X0 (X0_out, A0, B0);
  and \and  (and_out, A3, ~B3);  // AND_Gate
  and and_2 (and_2_out, X3_out, A2, ~B2);  // AND_Gate
  and and_3 (and_3_out, X3_out, X2_out, A1, ~B1);  // AND_Gate
  and and_4 (and_4_out, X3_out, X2_out, X1_out, A0, ~B0);  // AND_Gate
  and u_A_B (A_B, X3_out, X2_out, X1_out, X0_out);
  or u_A_B_2 (A_B_2, and_out, and_2_out, and_3_out, and_4_out);
  and u_A_B_3 (A_B_3, ~A_B, ~A_B_2);  // AND_Gate
endmodule

module Jogo (
  input  [3:0] in_1,
  input  Jogar,
  input  [3:0] in_3,
  input  Selecionar_jogador,
  output Correto,
  output \Número_secreto_é_menor ,
  output \Número_secreto_é_maior 
);

  wire _0_c, _1_c, _2_c, _3_c, comparador_1_a_b, comparador_1_a_b_2, comparador_1_a_b_3;

  Mux_2_1 _0 (.Sel(Selecionar_jogador), .B(in_3[0]), .A(in_1[0]), .C(_0_c));
  Mux_2_1 _1 (.Sel(Selecionar_jogador), .B(in_3[1]), .A(in_1[1]), .C(_1_c));
  Mux_2_1 _2 (.Sel(Selecionar_jogador), .B(in_3[2]), .A(in_1[2]), .C(_2_c));
  Mux_2_1 _3 (.Sel(Selecionar_jogador), .B(in_3[3]), .A(in_1[3]), .C(_3_c));
  Comparador comparador_1 (
    .A3(_3_c), .A2(_2_c), .A1(_1_c), .A0(_0_c), .B3(1'b1), .B2(1'b0), .B1(1'b1), .B0(1'b0),
    .A_B(comparador_1_a_b), .A_B_2(comparador_1_a_b_2), .A_B_3(comparador_1_a_b_3));
  and and_1 (Correto, Jogar, comparador_1_a_b);
  and and_2 (\Número_secreto_é_menor , Jogar, comparador_1_a_b_2);
  and and_3 (\Número_secreto_é_maior , Jogar, comparador_1_a_b_3);

  // Notes on the sheet:
  //   Jogador 0
  //   Jogador 1
  //   Número secreto
endmodule
